// Digital circuit Cpu.dig as structural Verilog
module Cpu (
  input  Clock,
  input  [15:0] BUS__Addr,
  input  [7:0] BUS__Memory,
  input  ResetIn,
  input  ShiftSelectA,
  input  ShiftSelectB,
  input  CarrySelectA,
  input  CarrySelectB
);

  wire ArithCarry, Control__MemBridge__Direction, Control__MemBridge__Load, Control__Reg__A__Assert,
       Control__Reg__A__LHS, Control__Reg__A__Load, Control__Reg__A__RHS, Control__Reg__B__Assert,
       Control__Reg__B__LHS, Control__Reg__B__Load, Control__Reg__B__RHS, Control__Reg__C__Assert,
       Control__Reg__C__LHS, Control__Reg__C__Load, Control__Reg__C__RHS, Control__Reg__D__Assert,
       Control__Reg__D__LHS, Control__Reg__D__Load, Control__Reg__D__RHS, Flags__0__Overflow, Flags__1__Sign,
       Flags__2__Zero, Flags__3__CarryA, Flags__4__CarryL, Flags__5__PCRA__Flip, Pipe0Out__0__Inc__PCRA0,
       Pipe0Out__1__Inc__PCRA1, Pipe1Out__0__LHS0, Pipe1Out__1__LHS1, Pipe1Out__2__RHS0, Pipe1Out__3__RHS1,
       Pipe1Out__8__Xfer__LoadDec0, Pipe1Out__9__Xfer__LoadDec1, Pipe1Out__10__Xfer__LoadDec2,
       Pipe1Out__11__Xfer__LoadDec3, Pipe1Out__12__Xfer__Assert0, Pipe1Out__13__Xfer__Assert1,
       Pipe1Out__14__Xfer__Assert2, Pipe1Out__15__FetchSuppress, Pipe2Out__0__MainBus__Assert0,
       Pipe2Out__1__MainBus__Assert1, Pipe2Out__2__MainBus__Assert2, Pipe2Out__3__MainBus__Assert3,
       Pipe2Out__4__MainBus__Load0, Pipe2Out__5__MainBus__Load1, Pipe2Out__6__MainBus__Load2,
       Pipe2Out__7__MainBus__Load3, Pipe2Out__8__Inc__SPSIDI0, Pipe2Out__9__Inc__SPSIDI1,
       Pipe2Out__10__AddrSel0, Pipe2Out__11__AddrSel1, Pipe2Out__12__AddrSel2, Pipe2Out__13__BusRequest,
       Pipe2Out__15__Break, Shift__CarryOut;
  wire [7:0] Bus__LHS, Bus__Main, Bus__RHS, Data, Pipe0Out__Pipeline, Pipe1Out__Pipeline, Pipe2Out__Pipeline,
       Shift__LHSOut;

  flags Flags (
    .ClockIn(Clock), .ArithCarryIn(ArithCarry), .DataIn(Data), .LogicCarryIn(Shift__CarryOut),
    .LHS(Bus__LHS), .RHS(Bus__RHS));  // open: ArithCarryFlag, ZeroFlag, LogicCarryFlag, SignFlag, OverflowFlag
  reg_8bit_generalpurpose A (
    .MainBusIn(Bus__Main), .Reg__Assert__RHS(Control__Reg__A__RHS), .Reg__Assert__LHS(Control__Reg__A__LHS),
    .Reg__Assert(Control__Reg__A__Assert), .Reg__Load(Control__Reg__A__Load), .MainBusOut(Bus__Main),
    .LHSBus(Bus__LHS), .RHSBus(Bus__RHS));  // open: RegisterContents
  reg_8bit_generalpurpose B (
    .MainBusIn(Bus__Main), .Reg__Assert__RHS(Control__Reg__B__RHS), .Reg__Assert__LHS(Control__Reg__B__LHS),
    .Reg__Assert(Control__Reg__B__Assert), .Reg__Load(Control__Reg__B__Load), .MainBusOut(Bus__Main),
    .LHSBus(Bus__LHS), .RHSBus(Bus__RHS));  // open: RegisterContents
  reg_8bit_generalpurpose C (
    .MainBusIn(Bus__Main), .Reg__Assert__RHS(Control__Reg__C__RHS), .Reg__Assert__LHS(Control__Reg__C__LHS),
    .Reg__Assert(Control__Reg__C__Assert), .Reg__Load(Control__Reg__C__Load), .MainBusOut(Bus__Main),
    .LHSBus(Bus__LHS), .RHSBus(Bus__RHS));  // open: RegisterContents
  reg_8bit_generalpurpose D (
    .MainBusIn(Bus__Main), .Reg__Assert__RHS(Control__Reg__D__RHS), .Reg__Assert__LHS(Control__Reg__D__LHS),
    .Reg__Assert(Control__Reg__D__Assert), .Reg__Load(Control__Reg__D__Load), .MainBusOut(Bus__Main),
    .LHSBus(Bus__LHS), .RHSBus(Bus__RHS));  // open: RegisterContents
  // memory memory_1: pin names not known; wires that end beside it: Control__MemBridge__Direction, Control__MemBridge__Load, BUS__Addr, BUS__Memory, BUS__Addr, BUS__Memory
  adder adder_1 (
    .ClockIn(Clock), .CarryFlag(Flags__3__CarryA), .LHS(Shift__LHSOut), .RHS(Bus__RHS),
    .CarrySelectA(CarrySelectA), .CarrySelectB(CarrySelectB), .CarryOut(ArithCarry), .AdderOut(Data));
  shift LHS_Shift (
    .SelectA(ShiftSelectA), .SelectB(ShiftSelectB), .LHSIn(Bus__LHS), .CarryIn(Flags__4__CarryL),
    .CarryOut(Shift__CarryOut), .LHSOut(Shift__LHSOut));
  pipeline_stage2 Stage_2 (
    .ClockIn(Clock), .Flags__0__Overflow(Flags__0__Overflow), .Flags__1__Sign(Flags__1__Sign),
    .Flags__2__Zero(Flags__2__Zero), .Flags__3__CarryA(Flags__3__CarryA),
    .Flags__4__CarryL(Flags__4__CarryL), .Flags__5__PCRA__Flip(Flags__5__PCRA__Flip),
    .Flags__6__Reset(ResetIn), .PipeIn(Pipe1Out__Pipeline), .PipeOut(Pipe2Out__Pipeline),
    .Pipe2Out__0__MainAssert0(Pipe2Out__0__MainBus__Assert0),
    .Pipe2Out__1__MainAssert1(Pipe2Out__1__MainBus__Assert1),
    .Pipe2Out__2__MainAssert2(Pipe2Out__2__MainBus__Assert2),
    .Pipe2Out__3__MainAssert3(Pipe2Out__3__MainBus__Assert3),
    .Pipe2Out__4__MainLoad0(Pipe2Out__4__MainBus__Load0),
    .Pipe2Out__5__MainLoad1(Pipe2Out__5__MainBus__Load1),
    .Pipe2Out__6__MainLoad2(Pipe2Out__6__MainBus__Load2),
    .Pipe2Out__7__MainLoad3(Pipe2Out__7__MainBus__Load3), .Pipe2Out__8__Inc0(Pipe2Out__8__Inc__SPSIDI0),
    .Pipe2Out__9__Inc1(Pipe2Out__9__Inc__SPSIDI1), .Pipe2Out__10__Addr0(Pipe2Out__10__AddrSel0),
    .Pipe2Out__11__Addr1(Pipe2Out__11__AddrSel1), .Pipe2Out__12__Addr2(Pipe2Out__12__AddrSel2),
    .Pipe2Out__13__BusRequest(Pipe2Out__13__BusRequest), .Pipe2Out__14__PCRA__Flip(Flags__5__PCRA__Flip),
    .Pipe2Out__15__Break(Pipe2Out__15__Break));
  pipeline_stage1 Stage_1 (
    .ClockIn(Clock), .BusRequest(Pipe2Out__13__BusRequest), .Flags__0__Overflow(Flags__0__Overflow),
    .Flags__1__Sign(Flags__1__Sign), .Flags__2__Zero(Flags__2__Zero), .Flags__3__CarryA(Flags__3__CarryA),
    .Flags__4__CarryL(Flags__4__CarryL), .Flags__5__PCRA__Flip(Flags__5__PCRA__Flip),
    .Flags__6__Reset(ResetIn), .PipeIn(Pipe0Out__Pipeline), .PipeOut(Pipe1Out__Pipeline),
    .Pipe1Out__0__LHS0(Pipe1Out__0__LHS0), .Pipe1Out__1__LHS1(Pipe1Out__1__LHS1),
    .Pipe1Out__2__RHS0(Pipe1Out__2__RHS0), .Pipe1Out__3__RHS1(Pipe1Out__3__RHS1),
    .Pipe1Out__8__XLD0(Pipe1Out__8__Xfer__LoadDec0), .Pipe1Out__9__XLD1(Pipe1Out__9__Xfer__LoadDec1),
    .Pipe1Out__10__XLD2(Pipe1Out__10__Xfer__LoadDec2), .Pipe1Out__11__XLD3(Pipe1Out__11__Xfer__LoadDec3),
    .Pipe1Out__12__XA0(Pipe1Out__12__Xfer__Assert0), .Pipe1Out__13__XA1(Pipe1Out__13__Xfer__Assert1),
    .Pipe1Out__14__XA2(Pipe1Out__14__Xfer__Assert2), .Pipe1Out__15__FetchSuppress(Pipe1Out__15__FetchSuppress));  // open: Pipe1Out__4__ALUOP0, Pipe1Out__5__ALUOP1, Pipe1Out__6__ALUOP2, Pipe1Out__7__ALUOP3
  pipeline_stage0 Stage_0 (
    .MEMDATA(BUS__Memory), .BusRequest(Pipe2Out__13__BusRequest),
    .FetchSuppress(Pipe1Out__15__FetchSuppress), .Flags__5__PCRA__Flip(Flags__5__PCRA__Flip),
    .ClockIn(Clock), .Pipe0Out(Pipe0Out__Pipeline), .Pipe0Out__0__IncPCRA0(Pipe0Out__0__Inc__PCRA0),
    .Pipe0Out__1__IncPCRA1(Pipe0Out__1__Inc__PCRA1));
  // buscontrol Bus_Control: pin names not known; wires that end beside it: Clock, ResetIn, Pipe2Out__0__MainBus__Assert0, Pipe2Out__1__MainBus__Assert1, Pipe2Out__2__MainBus__Assert2, Pipe2Out__3__MainBus__Assert3, Pipe2Out__4__MainBus__Load0, Pipe2Out__5__MainBus__Load1, Pipe2Out__6__MainBus__Load2, Pipe2Out__7__MainBus__Load3, Pipe2Out__8__Inc__SPSIDI0, Pipe2Out__9__Inc__SPSIDI1, Pipe2Out__10__AddrSel0, Pipe2Out__11__AddrSel1, Pipe2Out__12__AddrSel2, Pipe1Out__0__LHS0, Pipe1Out__1__LHS1, Pipe1Out__2__RHS0, Pipe1Out__3__RHS1, Pipe1Out__12__Xfer__Assert0, Pipe1Out__13__Xfer__Assert1, Pipe1Out__14__Xfer__Assert2, Pipe1Out__8__Xfer__LoadDec0, Pipe1Out__9__Xfer__LoadDec1, Pipe1Out__10__Xfer__LoadDec2, Pipe1Out__11__Xfer__LoadDec3, Pipe0Out__0__Inc__PCRA0, Pipe0Out__1__Inc__PCRA1, Control__Reg__A__LHS, Control__Reg__B__LHS, Control__Reg__C__LHS, Control__Reg__D__LHS, Control__Reg__A__RHS, Control__Reg__B__RHS, Control__Reg__C__RHS, Control__Reg__D__RHS, Control__Reg__A__Assert, Control__Reg__B__Assert, Control__Reg__C__Assert

  // Other names for the same wires on the sheet: Flags__6__Reset = ResetIn;
  //   Pipe2Out__14__PCRA__Flip = Flags__5__PCRA__Flip

  // Notes on the sheet:
  //   Registers
  //   ALU
  //   Pipeline / Control
endmodule
